# Fritzing sketch Sketch HC-SR04 (saved by Fritzing 0.9.3b)
breadboards: 1

parts:
  U1 = NodeMCU V1.0
  hc-sr1 = hc-sr04
  R1 = Resistor [tolerance=±5% resistance=220 package=THT]
  LED1 = LED - 5mm [color="Red (633nm)" package="5 mm [THT]"]
  LED2 = LED - 5mm [color="Red (633nm)" package="5 mm [THT]"]
  R2 = Resistor [tolerance=±5% resistance=220 package=THT]

nets:
  N1: U1.D0, hc-sr1.Trig
  N2: U1.D1, hc-sr1.Echo
  N3: U1.D2, LED1.anode
  N4: U1.D3, LED2.anode
  3V3: U1.3V3, hc-sr1.VCC
  GND: U1.GND, hc-sr1.GND, R1.Pin_0, R2.Pin_0
  N5: R1.Pin_1, LED1.cathode
  N6: LED2.cathode, R2.Pin_1

custom parts:
  NodeMCU V1.0: ESP8266 based NodeMCU
